// Logisim project 4bit_cpu.circ as structural Verilog
module CPU1 (
  input  in_1,
  output overflow,
  output carry,
  output zero,
  output Negative,
  output [3:0] out_6,
  output [15:0] out_7
);

  wire clk, Data, load, MoveImmd, or_1_out, or_2_out, store;
  wire [2:0] controlled_buffer_4_out;
  wire [3:0] alu_1_y, controlled_buffer_1_out, controlled_buffer_2_out, ram_1_dout, registerfile_1_out_a,
       registerfile_1_out_b;
  wire [7:0] Program_Counter_q;
  wire [15:0] rom_1_data;

  RAM #(.addrWidth(10), .dataWidth(4), .enables("line")) ram_1 (
    .addr(out_7[12:3]), .we(store), .clk(clk), .din(controlled_buffer_1_out), .dout(ram_1_dout));
  Clock clock_1 (.out(clk));
  Counter Program_Counter (
    .clr(in_1), .load(1'b0), .up(1'b1), .count(1'b1), .clk(clk), .Q(Program_Counter_q));  // open: D, carry
  assign controlled_buffer_1_out = store ? registerfile_1_out_b : 4'bz;  // Controlled_Buffer controlled_buffer_1
  assign controlled_buffer_2_out = MoveImmd ? out_7[6:3] : 4'bz;  // Controlled_Buffer controlled_buffer_2
  ROM #(.dataWidth(16)) rom_1 (.addr(Program_Counter_q), .data(rom_1_data));
  assign controlled_buffer_2_out = load ? ram_1_dout : 4'bz;  // Controlled_Buffer controlled_buffer_3
  or or_1 (or_1_out, load, Data, MoveImmd);
  assign controlled_buffer_4_out = store ? out_7[2:0] : 3'bz;  // Controlled_Buffer controlled_buffer_4
  Register #(.width(16)) IR (.D(rom_1_data), .en(1'b1), .clk(clk), .Q(out_7));  // open: clr
  assign controlled_buffer_2_out = Data ? alu_1_y : 4'bz;  // Controlled_Buffer controlled_buffer_5
  assign controlled_buffer_4_out = or_2_out ? out_7[5:3] : 3'bz;  // Controlled_Buffer controlled_buffer_6
  or or_2 (or_2_out, Data, MoveImmd, load);
  and and_1 (Data, ~out_7[15], ~out_7[14], out_7[13]);  // AND_Gate
  and and_2 (MoveImmd, ~out_7[15], out_7[14], out_7[13]);  // AND_Gate
  and and_3 (load, out_7[15], out_7[14], ~out_7[13]);  // AND_Gate
  and and_4 (store, out_7[15], ~out_7[14], out_7[13]);  // AND_Gate
  RegisterFile registerfile_1 (
    .CLK(clk), .Write(or_1_out), .IN_VAL(controlled_buffer_2_out), .Rd(out_7[2:0]), .Ra(out_7[8:6]),
    .Rb(controlled_buffer_4_out), .OUT_A(registerfile_1_out_a), .OUT_B(registerfile_1_out_b));
  ALU alu_1 (
    .A(registerfile_1_out_a), .B(registerfile_1_out_b), .OP(out_7[12:9]), .Y(alu_1_y), .O(overflow),
    .C(carry), .Z(zero), .N(Negative));
  Register #(.width(4)) flag (.D({Negative, zero, carry, overflow}), .en(Data), .clk(clk), .Q(out_6));  // open: clr

  // Other names for the same wires on the sheet: Addr[9:0] = out_7[12:3]; Rb[2:0] = out_7[5:3];
  //   value[3:0] = out_7[6:3]; Ra[2:0] = out_7[8:6]; op[3:0] = out_7[12:9]; Rd[2:0] = out_7[2:0]

  // Notes on the sheet:
  //   System Clock
  //   contents of rom_1 (hex, n*v repeats v):
  //   c000 6031 200a a00a 220b a013 300c a01c 3c25
  //   OP Code
  //   ADD - 0000
  //   SUB - 0001
  //   AND - 1000
  //   OR - 1010
  //   XOR - 1100
  //   Instruction Format
  //   MOV - 1110 (Rb is moved to Rd)
  //   op Ra, Rb, Rd  [001o oooa aabb bddd]
  //   moveImmd #4bit_no , Rd   [0110 0000 0VVV VRRR]
  //   LDR [loc] , Rd   [110A AAAA AAAA ARRR]
  //   STR Rb, [loc]   [101A AAAA AAAA ARRR]
endmodule

module RegisterFile (
  input  CLK,
  input  Write,
  input  [3:0] IN_VAL,
  input  [2:0] Rd,
  input  [2:0] Ra,
  input  [2:0] Rb,
  output [3:0] OUT_A,
  output [3:0] OUT_B
);

  wire demultiplexer_1_out0, demultiplexer_1_out1, demultiplexer_1_out2, demultiplexer_1_out3,
       demultiplexer_1_out4, demultiplexer_1_out5, demultiplexer_1_out6, demultiplexer_1_out7;
  wire [3:0] R0_q, R1_q, R2_q, R3_q, R4_q, R5_q, R6_q, R7_q;

  Demultiplexer #(.select(3)) demultiplexer_1 (
    .out0(demultiplexer_1_out0), .out1(demultiplexer_1_out1), .out2(demultiplexer_1_out2),
    .out3(demultiplexer_1_out3), .out4(demultiplexer_1_out4), .out5(demultiplexer_1_out5),
    .out6(demultiplexer_1_out6), .out7(demultiplexer_1_out7), .in(Write), .sel(Rd));
  Register #(.width(4)) R0 (.D(IN_VAL), .en(demultiplexer_1_out0), .clk(CLK), .Q(R0_q));  // open: clr
  Register #(.width(4)) R1 (.D(IN_VAL), .en(demultiplexer_1_out1), .clk(CLK), .Q(R1_q));  // open: clr
  Register #(.width(4)) R2 (.D(IN_VAL), .en(demultiplexer_1_out2), .clk(CLK), .Q(R2_q));  // open: clr
  Register #(.width(4)) R3 (.D(IN_VAL), .en(demultiplexer_1_out3), .clk(CLK), .Q(R3_q));  // open: clr
  Register #(.width(4)) R4 (.D(IN_VAL), .en(demultiplexer_1_out4), .clk(CLK), .Q(R4_q));  // open: clr
  Register #(.width(4)) R5 (.D(IN_VAL), .en(demultiplexer_1_out5), .clk(CLK), .Q(R5_q));  // open: clr
  Register #(.width(4)) R6 (.D(IN_VAL), .en(demultiplexer_1_out6), .clk(CLK), .Q(R6_q));  // open: clr
  Register #(.width(4)) R7 (.D(IN_VAL), .en(demultiplexer_1_out7), .clk(CLK), .Q(R7_q));  // open: clr
  Multiplexer #(.select(3), .width(4)) multiplexer_1 (
    .in0(R0_q), .in1(R1_q), .in2(R2_q), .in3(R3_q), .in4(R4_q), .in5(R5_q), .in6(R6_q), .in7(R7_q),
    .out(OUT_A), .sel(Ra));
  Multiplexer #(.select(3), .width(4)) multiplexer_2 (
    .in0(R0_q), .in1(R1_q), .in2(R2_q), .in3(R3_q), .in4(R4_q), .in5(R5_q), .in6(R6_q), .in7(R7_q),
    .out(OUT_B), .sel(Rb));
endmodule

module add_sub (
  input  [3:0] A,
  input  [3:0] B,
  input  Cin,
  output [3:0] S,
  output o,
  output Cout
);

  wire adder_1_cout, adder_2_cout, adder_3_cout, xor_1_out, xor_2_out, xor_3_out, xor_4_out;

  xor xor_1 (xor_1_out, Cin, B[0]);
  xor xor_2 (xor_2_out, Cin, B[1]);
  xor xor_3 (xor_3_out, Cin, B[2]);
  xor xor_4 (xor_4_out, Cin, B[3]);
  Adder #(.width(1)) adder_1 (.a(A[0]), .b(xor_1_out), .out(S[0]), .cin(Cin), .cout(adder_1_cout));
  Adder #(.width(1)) adder_2 (.a(A[1]), .b(xor_2_out), .out(S[1]), .cin(adder_1_cout), .cout(adder_2_cout));
  Adder #(.width(1)) adder_3 (.a(A[2]), .b(xor_3_out), .out(S[2]), .cin(adder_2_cout), .cout(adder_3_cout));
  Adder #(.width(1)) adder_4 (.a(A[3]), .b(xor_4_out), .out(S[3]), .cin(adder_3_cout), .cout(Cout));
  xor xor_5 (o, adder_3_cout, Cout);

  // Notes on the sheet:
  //   a
  //   b
endmodule

module LOGIC_UNIT (
  input  [3:0] a,
  input  [3:0] b,
  input  [1:0] f,
  output [3:0] y
);

  wire [3:0] and_1_out, or_1_out, xor_1_out;

  assign and_1_out = a & b;  // AND_Gate and_1, 4 bits wide
  assign or_1_out = a | b;  // OR_Gate or_1, 4 bits wide
  assign xor_1_out = a ^ b;  // XOR_Gate xor_1, 4 bits wide
  Multiplexer #(.select(2), .width(4)) multiplexer_1 (
    .in0(and_1_out), .in1(or_1_out), .in2(xor_1_out), .in3(b), .out(y), .sel(f));
endmodule

module ALU (
  input  [3:0] A,
  input  [3:0] B,
  input  [3:0] OP,
  output [3:0] Y,
  output O,
  output C,
  output Z,
  output N
);

  wire [3:0] add_sub_1_s, logic_unit_1_y;

  add_sub add_sub_1 (.A(A), .B(B), .Cin(OP[0]), .S(add_sub_1_s), .o(O), .Cout(C));
  LOGIC_UNIT logic_unit_1 (.a(A), .b(B), .f(OP[2:1]), .y(logic_unit_1_y));
  Multiplexer #(.width(4)) multiplexer_1 (.in0(add_sub_1_s), .in1(logic_unit_1_y), .out({N, Y[2:0]}), .sel(OP[3]));
  nor nor_1 (Z, Y[0], Y[1], Y[2], N);

  assign Y[3] = N;
endmodule
